// Logisim project Lab03_PrEncoder.circ as structural Verilog: 2 circuits, main circuit main
module main (
  input  in_1,
  input  in_2,
  input  in_3,
  input  in_4,
  input  in_5,
  input  in_6,
  input  in_7,
  input  in_8,
  input  in_9,
  output [3:0] out_10
);

  Encoder encoder_1 (
    .In1(in_1), .In2(in_2), .In3(in_3), .In4(in_4), .In5(in_5), .In6(in_6), .In7(in_7), .In8(in_8),
    .In9(in_9), .Out1(out_10[0]), .Out2(out_10[1]), .Out3(out_10[2]), .Out4(out_10[3]));
  Hex_Digit_Display hex_digit_display_1 (.value(out_10));  // open: dp

  // Notes on the sheet:
  //   Dinmukhamed_Lab03_15.02.25
endmodule

module Encoder (
  input  In1,
  input  In2,
  input  In3,
  input  In4,
  input  In5,
  input  In6,
  input  In7,
  input  In8,
  input  In9,
  output Out1,
  output Out2,
  output Out3,
  output Out4
);

  wire u1_out, u2_out, u3_out, u4_out, u5_out, u6_out, u7_out, u8_out, u9_out, u10_out, u11_out, u12_out,
       u16_out;

  nor u16 (u16_out, In8, In9);
  and u1 (u1_out, In1, ~In2, ~In4, ~In6, u16_out);  // AND_Gate
  and u2 (u2_out, In3, ~In4, ~In6, u16_out);  // AND_Gate
  and u3 (u3_out, In5, ~In6, u16_out);  // AND_Gate
  and u4 (u4_out, In7, u16_out);
  and u5 (u5_out, In2, ~In4, ~In5, u16_out);  // AND_Gate
  and u6 (u6_out, ~In4, ~In5, In3, u16_out);  // AND_Gate
  and u7 (u7_out, In6, u16_out);
  and u8 (u8_out, In7, u16_out);
  and u9 (u9_out, In4, u16_out);
  and u10 (u10_out, In5, u16_out);
  and u11 (u11_out, In6, u16_out);
  and u12 (u12_out, In7, u16_out);
  or u13 (Out1, u1_out, u2_out, u3_out, u4_out, In9);
  or u14 (Out2, u5_out, u6_out, u7_out, u8_out);
  or u15 (Out3, u9_out, u10_out, u11_out, u12_out);
  or u17 (Out4, In9, In8);
endmodule
